// Logisim project CS257_S1_Q1.circ as structural Verilog: 1 circuit, main circuit main
module main (
  input  A,
  input  B,
  output A_B,
  output n_A_B
);

  and and_1 (A_B, A, B);
  nor nor_1 (n_A_B, A, B);

  // Notes on the sheet:
  //   s1-q1
  //   roll no: 211cs257
  //   name: shivam yadav
  //   q: verification of truth table of AND , NOR gate
  //   AND GATE
  //   NOR GATE
endmodule
