// Logisim project CS257_S2_Q1.circ as structural Verilog: 1 circuit, main circuit main
module main (
  input  x,
  input  y,
  input  z,
  output F
);

  wire and_1_out, and_2_out, not_1_out, not_2_out;

  not not_1 (not_1_out, x);
  not not_2 (not_2_out, y);
  and and_1 (and_1_out, not_1_out, y);
  and and_2 (and_2_out, x, not_2_out);
  nor nor_1 (F, and_1_out, and_2_out, z);

  // Notes on the sheet:
  //   s2-q1
  //   name: shivam yadav
  //   roll no: 211cs257
  //   = ~((X^Y)|z)
endmodule
